# Fritzing sketch micro_sunboard_esp32 (saved by Fritzing 0.9.4)
circuit board: 8.46667cm x 5.64444cm

parts:
  clema_led_5v = Screw terminal - 2 pins [package=THT]
  clema_led_tierra = Screw terminal - 2 pins [package=THT]
  clema_led_datos = Screw terminal - 2 pins [package=THT]
  dc_jack = Power Jack [package=power_jack_pth_lock]
  R1 = Resistor [tolerance=±5% resistance=470 package=THT]
  C1 = Electrolytic Capacitor [capacitance=100µF package="100 mil [THT, electrolytic]"]
  on_off_switch = Toggle Switch [package=THT]
  R5 = Resistor [tolerance=±5% resistance=470 package=THT]
  led_on/off = LED - 5mm [color="Red (633nm)" package="5 mm [THT]"]
  led_bt = LED - 5mm [color="Red (633nm)" package="5 mm [THT]"]
  R6 = Resistor [tolerance=±5% resistance=470 package=THT]
  reset = Pushbutton [package=THT]
  U1 = ESP32S-HiLetgo [part_number=ESP32S-HiLetgo]

nets:
  N1: clema_led_5v.pin1, clema_led_5v.pin2, dc_jack.PWR, C1.+, led_on/off.anode, U1.VIN
  N2: clema_led_tierra.pin1, clema_led_tierra.pin2, C1.-, on_off_switch.COM, R5.Pin_0, R5.Pin_1, led_on/off.cathode, R6.Pin_1, reset.leg0, U1.GND
  N3: clema_led_datos.pin1, R1.Pin_1
  N4: dc_jack.GND, on_off_switch.L2
  N5: R1.Pin_0, U1.GPIO4
  N6: led_bt.cathode, R6.Pin_0
  N7: led_bt.anode, U1.GPIO0
  N8: reset.leg1, U1.EN

notes:
  SunBoard Led System, 1.0

custom parts:
  ESP32S-HiLetgo: HiLetgo ESP-WROOM-32 ESP32 ESP-32S Development Board 2.4GHz Dual-Mode WiFi + Bluetooth Dual Cores Microcontroller The ESP32 integrated with Antenna switches, RF Balun, power amplifiers, low-noise amplifiers, filters, and management modules, and the entire solution occupies the least area of PCB. 2.4 GHz Wi-Fi plus Bluetooth dual-mode chip, with TSMC Ultra-low power consumption 40nm technology,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
